// Logisim project Logisim_fibonacci.circ as structural Verilog: 3 circuits, main circuit main
module main (
  input  [2:0] \input ,
  output [3:0] \output 
);

  wire clock, comparator_1_eq, not_1_out, work;
  wire [2:0] counter_1_q;
  wire [3:0] adder_1_out, F_x_1_q, F_x_2_q, multiplexer_1_out;

  not not_1 (not_1_out, comparator_1_eq);
  Comparator #(.width(4), .mode("unsigned")) comparator_1 (
    .a(4'b0000), .b(adder_1_out), .eq(comparator_1_eq));  // open: gt, lt
  Counter #(.width(3), .max('h7), .ongoal("stay")) counter_1 (
    .Q(counter_1_q), .clk(clock));  // open: load, D, count, carry, clr
  Multiplexer #(.width(4)) multiplexer_1 (
    .in0(4'b0001), .in1(adder_1_out), .out(multiplexer_1_out), .sel(not_1_out));  // open: en
  Clock clock_1 (.out(clock));
  // Probe on counter_1_q
  Comparator #(.width(3), .mode("unsigned")) comparator_2 (.a(counter_1_q), .b(\input ), .lt(work));  // open: gt, eq
  Register #(.width(4)) F_x_1 (.D(multiplexer_1_out), .en(work), .Q(F_x_1_q), .clk(clock));  // open: clr
  Register #(.width(4)) F_x_2 (.D(F_x_1_q), .en(work), .Q(F_x_2_q), .clk(clock));  // open: clr
  Adder #(.width(4)) adder_1 (.a(F_x_1_q), .b(F_x_2_q), .out(adder_1_out));  // open: cin, cout
  // Probe on adder_1_out
  Multiplexer #(.width(4)) multiplexer_2 (.in0(F_x_1_q), .in1(4'b0000), .out(\output ), .sel(work));  // open: en
endmodule

module anonther (
  input  [31:0] \input 
);

  wire bitselector_1_out, clock_1_out, counter_1_q;
  wire [31:0] multiplexer_1_out, register_1_q, shifter_1_out;

  Register ans_x ();  // open: D, en, Q, clk, clr
  Multiplexer #(.width(32)) multiplexer_1 (
    .in0(\input ), .in1(shifter_1_out), .out(multiplexer_1_out), .sel(counter_1_q));  // open: en
  Counter #(.width(1), .max('h1), .ongoal("stay")) counter_1 (
    .Q(counter_1_q), .clk(clock_1_out));  // open: load, D, count, carry, clr
  Clock clock_1 (.out(clock_1_out));
  Register ans_y ();  // open: D, en, Q, clk, clr
  Register ans_z ();  // open: D, en, Q, clk, clr
  Register #(.width(32)) register_1 (.D(multiplexer_1_out), .Q(register_1_q), .clk(clock_1_out));  // open: en, clr
  Register temp_x ();  // open: D, en, Q, clk, clr
  BitSelector #(.width(32)) bitselector_1 (.in(register_1_q), .out(bitselector_1_out), .sel({5{1'b0}}));
  Shifter #(.width(32), .shift("lr")) shifter_1 (.in(register_1_q), .\dist (5'b00001), .out(shifter_1_out));
  Register temp_y ();  // open: D, en, Q, clk, clr
  Register temp_z ();  // open: D, en, Q, clk, clr
  matrix_multiply matrix_multiply_1 ();  // open: x1, y1, z1, x2, y2, z2, x3, y3, z3
endmodule

module matrix_multiply (
  input  [31:0] x1,
  input  [31:0] y1,
  input  [31:0] z1,
  input  [31:0] x2,
  input  [31:0] y2,
  input  [31:0] z2,
  output [31:0] x3,
  output [31:0] y3,
  output [31:0] z3
);

  wire [31:0] multiplier_1_cout, multiplier_1_out, multiplier_2_out, multiplier_3_cout, multiplier_3_out,
       multiplier_4_out, multiplier_5_cout, multiplier_5_out, multiplier_6_out;

  Multiplier #(.width(32)) multiplier_1 (
    .a(x1), .b(x2), .out(multiplier_1_out), .cout(multiplier_1_cout));  // open: cin
  Multiplier #(.width(32)) multiplier_2 (
    .a(y1), .b(y2), .out(multiplier_2_out), .cin(multiplier_1_cout));  // open: cout
  Multiplier #(.width(32)) multiplier_3 (
    .a(x1), .b(y2), .out(multiplier_3_out), .cout(multiplier_3_cout));  // open: cin
  Multiplier #(.width(32)) multiplier_4 (
    .a(y1), .b(z2), .out(multiplier_4_out), .cin(multiplier_3_cout));  // open: cout
  Multiplier #(.width(32)) multiplier_5 (
    .a(y1), .b(y2), .out(multiplier_5_out), .cout(multiplier_5_cout));  // open: cin
  Multiplier #(.width(32)) multiplier_6 (
    .a(z1), .b(z2), .out(multiplier_6_out), .cin(multiplier_5_cout));  // open: cout
  Adder #(.width(32)) adder_1 (.a(multiplier_1_out), .b(multiplier_2_out), .out(x3));  // open: cin, cout
  Adder #(.width(32)) adder_2 (.a(multiplier_3_out), .b(multiplier_4_out), .out(y3));  // open: cin, cout
  Adder #(.width(32)) adder_3 (.a(multiplier_5_out), .b(multiplier_6_out), .out(z3));  // open: cin, cout
endmodule
