// Logisim project Logisim_fibonacci2.circ as structural Verilog: 4 circuits, main circuit main
module main (
  input  [31:0] \input ,
  output [31:0] out_2
);

  wire clock_1_out, clock_2_out, clock_3_out, clock_4_out, clock_5_out, clock_6_out, clock_7_out,
       comparator_1_eq, multiplexer_2_out, sel, \time ;
  wire [31:0] ans_x_q, ans_y_q, ans_z_q, multiplexer_1_out, multiplexer_3_out, multiplexer_4_out,
       multiplexer_5_out, multiplexer_6_out, multiplexer_7_out, multiplexer_8_out, register_1_q,
       shifter_1_out, subtractor_1_out, t_x_prime, t_y_prime, t_z_prime, temp_x_q, temp_y_q, temp_z_q,
       x_prime, y_prime, z_prime;

  // Probe on \input 
  Multiplexer #(.width(32), .disabled(0), .enable("false")) multiplexer_1 (
    .in0(32'h1), .in1(x_prime), .out(multiplexer_1_out), .sel(\time ));
  Multiplexer #(.disabled(0), .enable("false")) multiplexer_2 (
    .in0(1'b1), .in1(sel), .out(multiplexer_2_out), .sel(\time ));
  Multiplexer #(.width(32), .disabled(0), .enable("false")) multiplexer_3 (
    .in0({32{1'b0}}), .in1(y_prime), .out(multiplexer_3_out), .sel(\time ));
  Multiplexer #(.width(32), .disabled(0), .enable("false")) multiplexer_4 (
    .in0(32'h1), .in1(t_x_prime), .out(multiplexer_4_out), .sel(\time ));
  Multiplexer #(.width(32), .disabled(0), .enable("false")) multiplexer_5 (
    .in0(32'h1), .in1(t_y_prime), .out(multiplexer_5_out), .sel(\time ));
  Subtractor #(.width(32)) subtractor_1 (.a(\input ), .b(32'h1), .out(subtractor_1_out));  // open: bin, bout
  Multiplexer #(.width(32)) multiplexer_6 (
    .in0(subtractor_1_out), .in1(shifter_1_out), .out(multiplexer_6_out), .sel(\time ));  // open: en
  Counter #(.width(1), .max('h1), .ongoal("stay")) counter_1 (
    .Q(\time ), .clk(clock_5_out));  // open: load, D, count, carry, clr
  Register #(.width(32)) ans_x (
    .D(multiplexer_1_out), .en(multiplexer_2_out), .Q(ans_x_q), .clk(clock_1_out));  // open: clr
  Clock clock_1 (.out(clock_1_out));
  Register #(.width(32)) ans_y (
    .D(multiplexer_3_out), .en(multiplexer_2_out), .Q(ans_y_q), .clk(clock_2_out));  // open: clr
  Clock clock_2 (.out(clock_2_out));
  Register #(.width(32)) temp_x (.D(multiplexer_4_out), .Q(temp_x_q), .clk(clock_3_out));  // open: en, clr
  Clock clock_3 (.out(clock_3_out));
  Register #(.width(32)) temp_y (.D(multiplexer_5_out), .Q(temp_y_q), .clk(clock_4_out));  // open: en, clr
  Clock clock_4 (.out(clock_4_out));
  Register #(.width(32)) register_1 (.D(multiplexer_6_out), .Q(register_1_q), .clk(clock_5_out));  // open: en, clr
  Clock clock_5 (.out(clock_5_out));
  Clock clock_6 (.out(clock_6_out));
  Multiplexer #(.width(32), .disabled(0), .enable("false")) multiplexer_7 (
    .in0(32'h1), .in1(z_prime), .out(multiplexer_7_out), .sel(\time ));
  BitSelector #(.width(32)) bitselector_1 (.in(register_1_q), .out(sel), .sel({5{1'b0}}));
  Shifter #(.width(32), .shift("lr")) shifter_1 (.in(register_1_q), .\dist (5'b00001), .out(shifter_1_out));
  Register #(.width(32)) ans_z (
    .D(multiplexer_7_out), .en(multiplexer_2_out), .Q(ans_z_q), .clk(clock_6_out));  // open: clr
  Multiplexer #(.width(32), .disabled(0), .enable("false")) multiplexer_8 (
    .in0({32{1'b0}}), .in1(t_z_prime), .out(multiplexer_8_out), .sel(\time ));
  Register #(.width(32)) temp_z (.D(multiplexer_8_out), .Q(temp_z_q), .clk(clock_7_out));  // open: en, clr
  Clock clock_7 (.out(clock_7_out));
  matrix_multiply matrix_multiply_1 (
    .x1(ans_x_q), .y1(ans_y_q), .z1(ans_z_q), .x2(temp_x_q), .y2(temp_y_q), .z2(temp_z_q), .x3(x_prime),
    .y3(y_prime), .z3(z_prime));
  Comparator #(.width(32)) comparator_1 (.a(register_1_q), .b({32{1'b0}}), .eq(comparator_1_eq));  // open: gt, lt
  matrix_multiply matrix_multiply_2 (
    .x1(temp_x_q), .y1(temp_y_q), .z1(temp_z_q), .x2(temp_x_q), .y2(temp_y_q), .z2(temp_z_q), .x3(t_x_prime),
    .y3(t_y_prime), .z3(t_z_prime));
  Multiplexer #(.width(32), .disabled(0)) multiplexer_9 (
    .in0({32{1'b0}}), .in1(ans_x_q), .out(out_2), .sel(comparator_1_eq));  // open: en
  // Probe on out_2
endmodule

module matrix_multiply (
  input  [31:0] x1,
  input  [31:0] y1,
  input  [31:0] z1,
  input  [31:0] x2,
  input  [31:0] y2,
  input  [31:0] z2,
  output [31:0] x3,
  output [31:0] y3,
  output [31:0] z3
);

  wire [31:0] multiplier_1_out, multiplier_2_out, multiplier_3_out, multiplier_4_out, multiplier_5_out,
       multiplier_6_out;

  Multiplier #(.width(32)) multiplier_1 (.a(x1), .b(x2), .out(multiplier_1_out));  // open: cin, cout
  Multiplier #(.width(32)) multiplier_2 (.a(y1), .b(y2), .out(multiplier_2_out));  // open: cin, cout
  Multiplier #(.width(32)) multiplier_3 (.a(x1), .b(y2), .out(multiplier_3_out));  // open: cin, cout
  Multiplier #(.width(32)) multiplier_4 (.a(y1), .b(z2), .out(multiplier_4_out));  // open: cin, cout
  Multiplier #(.width(32)) multiplier_5 (.a(y1), .b(y2), .out(multiplier_5_out));  // open: cin, cout
  Multiplier #(.width(32)) multiplier_6 (.a(z1), .b(z2), .out(multiplier_6_out));  // open: cin, cout
  Adder #(.width(32)) adder_1 (.a(multiplier_1_out), .b(multiplier_2_out), .out(x3));  // open: cin, cout
  Adder #(.width(32)) adder_2 (.a(multiplier_3_out), .b(multiplier_4_out), .out(y3));  // open: cin, cout
  Adder #(.width(32)) adder_3 (.a(multiplier_5_out), .b(multiplier_6_out), .out(z3));  // open: cin, cout
endmodule

// 0
module initialize_0 (
  input  [31:0] \input ,
  output [31:0] \output 
);

  wire clock_1_out, counter_1_q;

  Counter #(.width(1), .max('h1), .ongoal("stay")) counter_1 (
    .Q(counter_1_q), .clk(clock_1_out));  // open: load, D, count, carry, clr
  Clock clock_1 (.out(clock_1_out));
  Multiplexer #(.width(32)) multiplexer_1 (
    .in0({32{1'b0}}), .in1(\input ), .out(\output ), .sel(counter_1_q));  // open: en
endmodule

// 1
module initialize_1 (
  input  [31:0] \input ,
  output [31:0] \output 
);

  wire clock_1_out, counter_1_q;

  Counter #(.width(1), .max('h1), .ongoal("stay")) counter_1 (
    .Q(counter_1_q), .clk(clock_1_out));  // open: load, D, count, carry, clr
  Clock clock_1 (.out(clock_1_out));
  Multiplexer #(.width(32)) multiplexer_1 (.in0(32'h1), .in1(\input ), .out(\output ), .sel(counter_1_q));  // open: en
endmodule
