// Logisim project Logisim_mod5.circ as structural Verilog: 1 circuit, main circuit mod5
module mod5 (
  input  In,
  output S0,
  output S1,
  output S2,
  output S3,
  output S4
);

  wire and_2_out, and_3_out, clock_1_out, not_1_out, not_2_out, not_3_out;
  wire [2:0] or_1_out, register_1_q;

  not not_1 (not_1_out, In);
  not not_2 (not_2_out, In);
  not not_3 (not_3_out, register_1_q[1]);
  and and_1 (or_1_out[2], register_1_q[1], not_1_out);
  and and_2 (and_2_out, not_2_out, not_3_out);
  and and_3 (and_3_out, In, register_1_q[1]);
  or or_1 (or_1_out[0], and_2_out, and_3_out);
  // Probe on {or_1_out[2], In, or_1_out[0]}
  Register #(.width(3)) register_1 (
    .D({or_1_out[2], In, or_1_out[0]}), .Q(register_1_q), .clk(clock_1_out));  // open: en, clr
  Clock clock_1 (.out(clock_1_out));
  Decoder #(.select(3), .enable("false")) decoder_1 (
    .out0(S0), .out1(S1), .out2(S2), .out3(S3), .out4(S4), .sel({or_1_out[2], In, or_1_out[0]}));  // open: out5, out6, out7
endmodule
