// Logisim project SR Flip-Flop.circ as structural Verilog: 2 circuits, main circuit SR Flip-Flop or/not
module SR_Flip_Flop_or_not (
  input  R,
  input  S,
  output Q,
  output nQ
);

  wire or_1_out, or_2_out;

  or or_1 (or_1_out, R, nQ);
  not not_1 (Q, or_1_out);
  not not_2 (nQ, or_2_out);
  or or_2 (or_2_out, Q, S);
endmodule

module SR_Flip_Flop_and_not (
  input  R,
  input  S,
  output nQ,
  output Q
);

  wire and_1_out, and_2_out, not_1_out, not_2_out;

  not not_1 (not_1_out, R);
  and and_1 (and_1_out, not_1_out, Q);
  and and_2 (and_2_out, nQ, not_2_out);
  not not_2 (not_2_out, S);
  not not_3 (nQ, and_1_out);
  not not_4 (Q, and_2_out);
endmodule
