// Logisim project mod5.circ as structural Verilog: 2 circuits, main circuit mod5
module mod5 (
  input  In,
  output S0,
  output S1,
  output S2,
  output S3,
  output S4
);

  wire and_2_out, and_3_out, clock_1_out, not_1_out, not_2_out, not_3_out;
  wire [2:0] or_1_out, register_1_q;

  and and_1 (or_1_out[2], register_1_q[1], not_1_out);
  not not_1 (not_1_out, In);
  not not_2 (not_2_out, In);
  and and_2 (and_2_out, not_2_out, not_3_out);
  not not_3 (not_3_out, register_1_q[1]);
  and and_3 (and_3_out, In, register_1_q[1]);
  or or_1 (or_1_out[0], and_2_out, and_3_out);
  Clock clock_1 (.out(clock_1_out));
  Register #(.width(3)) register_1 (
    .D({or_1_out[2], In, or_1_out[0]}), .Q(register_1_q), .clk(clock_1_out));  // open: en, clr
  Decoder #(.select(3)) decoder_1 (
    .out0(S0), .out1(S1), .out2(S2), .out3(S3), .out4(S4), .sel({or_1_out[2], In, or_1_out[0]}));  // open: out5, out6, out7, en
endmodule

module _1 (
  input  n,
  output o2,
  output o1,
  output o0
);

  wire and_1_out, and_2_out, and_3_out, clock_1_out, clock_2_out, clock_3_out, not_1_out, not_2_out,
       not_3_out, or_1_out;

  not not_1 (not_1_out, n);
  not not_2 (not_2_out, n);
  not not_3 (not_3_out, o1);
  and and_1 (and_1_out, o1, not_1_out);
  and and_2 (and_2_out, not_2_out, not_3_out);
  and and_3 (and_3_out, n, o1);
  Register #(.width(1)) register_1 (.D(and_1_out), .Q(o2), .clk(clock_1_out));  // open: en, clr
  Clock clock_1 (.out(clock_1_out));
  Clock clock_2 (.out(clock_2_out));
  or or_1 (or_1_out, and_2_out, and_3_out);
  Clock clock_3 (.out(clock_3_out));
  Register #(.width(1)) register_2 (.D(n), .Q(o1), .clk(clock_2_out));  // open: en, clr
  Register #(.width(1)) register_3 (.D(or_1_out), .Q(o0), .clk(clock_3_out));  // open: en, clr
endmodule
