// Logisim project swap.circ as structural Verilog: 4 circuits, main circuit 1bit_swap
module _1bit_swap (
  input  I1,
  input  I2,
  input  S,
  output O1,
  output O2
);

  wire and_1_out, and_2_out, and_3_out, and_4_out, not_1_out, not_2_out;

  not not_1 (not_1_out, S);
  not not_2 (not_2_out, S);
  and and_1 (and_1_out, I1, not_1_out);
  and and_2 (and_2_out, I2, S);
  and and_3 (and_3_out, not_2_out, I2);
  and and_4 (and_4_out, I1, S);
  or or_1 (O1, and_1_out, and_2_out);
  or or_2 (O2, and_3_out, and_4_out);
endmodule

module _4bit_swap (
  input  [3:0] I1,
  input  [3:0] I2,
  input  S,
  output [3:0] O1,
  output [3:0] O2
);

  wire [3:0] and_1_out, and_2_out, and_3_out, and_4_out, bit_extender_1_out, not_1_out, not_2_out;

  assign bit_extender_1_out = {{3{S}}, S};  // Bit_Extender bit_extender_1
  assign not_1_out = ~bit_extender_1_out;  // NOT_Gate not_1, 4 bits wide
  assign not_2_out = ~bit_extender_1_out;  // NOT_Gate not_2, 4 bits wide
  assign and_1_out = I1 & not_1_out;  // AND_Gate and_1, 4 bits wide
  assign and_2_out = I2 & bit_extender_1_out;  // AND_Gate and_2, 4 bits wide
  assign and_3_out = not_2_out & I2;  // AND_Gate and_3, 4 bits wide
  assign and_4_out = I1 & bit_extender_1_out;  // AND_Gate and_4, 4 bits wide
  assign O1 = and_1_out | and_2_out;  // OR_Gate or_1, 4 bits wide
  assign O2 = and_3_out | and_4_out;  // OR_Gate or_2, 4 bits wide
endmodule

module _4bit_2change (
  input  [3:0] A,
  input  [3:0] B,
  output [3:0] A_prime,
  output [3:0] B_prime
);

  wire comparator_1_gt;

  Comparator #(.width(4), .mode("unsigned")) comparator_1 (.a(A), .b(B), .gt(comparator_1_gt));  // open: eq, lt
  _4bit_swap u_4bit_swap_1 (.I1(A), .I2(B), .S(comparator_1_gt), .O1(A_prime), .O2(B_prime));
endmodule

module _4bit_sort (
  input  [3:0] A,
  input  [3:0] B,
  input  [3:0] C,
  input  [3:0] D,
  output [3:0] _1,
  output [3:0] _2,
  output [3:0] _3,
  output [3:0] _4
);

  wire [3:0] n4bit_2change_1_a_prime, n4bit_2change_1_b_prime, n4bit_2change_2_a_prime,
       n4bit_2change_2_b_prime, n4bit_2change_3_a_prime, n4bit_2change_4_a_prime, n4bit_2change_4_b_prime,
       n4bit_2change_5_a_prime;

  _4bit_2change u_4bit_2change_1 (.A(A), .B(B), .A_prime(n4bit_2change_1_a_prime), .B_prime(n4bit_2change_1_b_prime));
  _4bit_2change u_4bit_2change_2 (
    .A(n4bit_2change_1_b_prime), .B(C), .A_prime(n4bit_2change_2_a_prime), .B_prime(n4bit_2change_2_b_prime));
  _4bit_2change u_4bit_2change_3 (.A(n4bit_2change_2_b_prime), .B(D), .A_prime(n4bit_2change_3_a_prime), .B_prime(_4));
  _4bit_2change u_4bit_2change_4 (
    .A(n4bit_2change_1_a_prime), .B(n4bit_2change_2_a_prime), .A_prime(n4bit_2change_4_a_prime),
    .B_prime(n4bit_2change_4_b_prime));
  _4bit_2change u_4bit_2change_5 (
    .A(n4bit_2change_4_b_prime), .B(n4bit_2change_3_a_prime), .A_prime(n4bit_2change_5_a_prime), .B_prime(_3));
  _4bit_2change u_4bit_2change_6 (.A(n4bit_2change_4_a_prime), .B(n4bit_2change_5_a_prime), .A_prime(_1), .B_prime(_2));
endmodule
