// Logisim project P0_L0_CRC.circ as structural Verilog: 3 circuits, main circuit CRC
module CRC (
  input  [7:0] A_data,
  input  [3:0] B_divisor,
  output [10:0] C_output
);

  wire [2:0] _4bit_mod2_2_remainder_3, _4bit_mod2_remainder_3, n4bit_mod2_1_remainder_3,
       n4bit_mod2_2_remainder_3, n4bit_mod2_3_remainder_3, n4bit_mod2_4_remainder_3, n4bit_mod2_5_remainder_3;
  wire [3:0] shifter_1_out_3, shifter_2_out_3, shifter_3_out_3, shifter_4_out_3, shifter_5_out_3,
       shifter_6_out_3, shifter_7_out_3;

  _4bit_mod2 u_4bit_mod2_1 (.dividend_4(A_data[7:4]), .divisor_4(B_divisor), .remainder_3(n4bit_mod2_1_remainder_3));
  shifter shifter_1 (._1(A_data[3]), ._3(n4bit_mod2_1_remainder_3), .out_3(shifter_1_out_3));
  _4bit_mod2 u_4bit_mod2_2 (
    .dividend_4(shifter_1_out_3), .divisor_4(B_divisor), .remainder_3(n4bit_mod2_2_remainder_3));
  shifter shifter_2 (._1(A_data[2]), ._3(n4bit_mod2_2_remainder_3), .out_3(shifter_2_out_3));
  _4bit_mod2 u_4bit_mod2_3 (
    .dividend_4(shifter_2_out_3), .divisor_4(B_divisor), .remainder_3(n4bit_mod2_3_remainder_3));
  shifter shifter_3 (._1(A_data[1]), ._3(n4bit_mod2_3_remainder_3), .out_3(shifter_3_out_3));
  _4bit_mod2 u_4bit_mod2_4 (
    .dividend_4(shifter_3_out_3), .divisor_4(B_divisor), .remainder_3(n4bit_mod2_4_remainder_3));
  shifter shifter_4 (._1(A_data[0]), ._3(n4bit_mod2_4_remainder_3), .out_3(shifter_4_out_3));
  _4bit_mod2 _4bit_mod2 (.dividend_4(shifter_4_out_3), .divisor_4(B_divisor), .remainder_3(_4bit_mod2_remainder_3));
  shifter shifter_5 (._1(1'b0), ._3(_4bit_mod2_remainder_3), .out_3(shifter_5_out_3));
  _4bit_mod2 u_4bit_mod2_5 (
    .dividend_4(shifter_5_out_3), .divisor_4(B_divisor), .remainder_3(n4bit_mod2_5_remainder_3));
  _4bit_mod2 _4bit_mod2_2 (.dividend_4(shifter_6_out_3), .divisor_4(B_divisor), .remainder_3(_4bit_mod2_2_remainder_3));
  shifter shifter_6 (._1(1'b0), ._3(n4bit_mod2_5_remainder_3), .out_3(shifter_6_out_3));
  shifter shifter_7 (._1(1'b0), ._3(_4bit_mod2_2_remainder_3), .out_3(shifter_7_out_3));
  _4bit_mod2 _4bit_mod2_3 (.dividend_4(shifter_7_out_3), .divisor_4(B_divisor), .remainder_3(C_output[2:0]));

  assign C_output[10:3] = A_data;

  // Other names for the same wires on the sheet: A[7:0] = A_data; ans_3[2:0] = C_output[2:0]
endmodule

module _4bit_mod2 (
  input  [3:0] dividend_4,
  input  [3:0] divisor_4,
  output [2:0] remainder_3
);

  wire [3:0] xor_1_out;

  assign xor_1_out = dividend_4 ^ divisor_4;  // XOR_Gate xor_1, 4 bits wide
  Multiplexer #(.width(3)) multiplexer_1 (
    .in0(dividend_4[2:0]), .in1(xor_1_out[2:0]), .out(remainder_3), .sel(dividend_4[3]));  // open: en
endmodule

module shifter (
  input  _1,
  input  [2:0] _3,
  output [3:0] out_3
);


  assign out_3 = {_3, _1};
endmodule
