// Logisim project P0_L0_FSM.circ as structural Verilog: 3 circuits, main circuit fsm
module fsm (
  input  [1:0] In,
  input  CLR,
  output out_3
);

  wire clock_1_out;
  wire [1:0] multiplexer_1_out, state_q, state_transition_1_s_0;

  state_transition state_transition_1 (
    .state_1(state_q[1]), .state_0(state_q[0]), .in_1(In[1]), .in_0(In[0]), .s_1(state_transition_1_s_0[1]),
    .s_0(state_transition_1_s_0[0]));
  Multiplexer #(.width(2)) multiplexer_1 (
    .in0(state_transition_1_s_0), .in1(2'b00), .out(multiplexer_1_out), .sel(CLR));  // open: en
  Register #(.width(2)) state (.D(multiplexer_1_out), .Q(state_q), .clk(clock_1_out));  // open: en, clr
  Clock clock_1 (.out(clock_1_out));
  \output  output_1 (.state_1(state_q[1]), .state_0(state_q[0]), .in_1(In[1]), .in_0(In[0]), .Z(out_3));
endmodule

module state_transition (
  input  state_1,
  input  state_0,
  input  in_1,
  input  in_0,
  output s_1,
  output s_0
);

  wire and_1_out, and_2_out, and_3_out, and_4_out, not_1_out, not_2_out, not_3_out, not_4_out, not_5_out,
       not_6_out, not_7_out;

  not not_1 (not_1_out, state_1);
  and and_1 (and_1_out, not_1_out, state_0, not_2_out);
  not not_2 (not_2_out, in_0);
  and and_2 (and_2_out, state_1, not_3_out, not_4_out);
  not not_3 (not_3_out, state_0);
  not not_4 (not_4_out, in_0);
  not not_5 (not_5_out, in_1);
  and and_3 (and_3_out, not_5_out, in_0);
  not not_6 (not_6_out, state_0);
  and and_4 (and_4_out, state_1, not_6_out, not_7_out);
  not not_7 (not_7_out, in_0);
  or or_1 (s_1, and_1_out, and_2_out);
  or or_2 (s_0, and_3_out, and_4_out);
endmodule

module \output  (
  input  state_1,
  input  state_0,
  input  in_1,
  input  in_0,
  output Z
);

  wire not_1_out, not_2_out;

  not not_1 (not_1_out, state_0);
  and and_1 (Z, state_1, not_1_out, not_2_out);
  not not_2 (not_2_out, in_0);
endmodule
