// Logisim project P0_L1_ftoi.circ as structural Verilog: 1 circuit, main circuit ftoi
module ftoi (
  input  [15:0] in_1,
  output [31:0] out_2
);

  wire comparator_1_eq, comparator_2_eq, or_1_out;
  wire [4:0] bit_extender_3_out, subtractor_1_out;
  wire [10:0] bit_extender_1_out;
  wire [31:0] bit_extender_2_out, buffer_1_out, multiplexer_1_out, negator_1_out, shifter_1_out,
       shifter_2_out;

  assign bit_extender_1_out = {{1{1'b1}}, in_1[9:0]};  // Bit_Extender bit_extender_1
  assign bit_extender_2_out = {{21{1'b0}}, bit_extender_1_out};  // Bit_Extender bit_extender_2
  Comparator #(.width(5)) comparator_1 (.a(in_1[14:10]), .b({5{1'b1}}), .eq(comparator_1_eq));  // open: gt, lt
  Subtractor #(.width(5)) subtractor_1 (.a(in_1[14:10]), .b(5'b01111), .out(subtractor_1_out));  // open: bin, bout
  Comparator #(.width(5)) comparator_2 (.a(in_1[14:10]), .b({5{1'b0}}), .eq(comparator_2_eq));  // open: gt, lt
  assign bit_extender_3_out = {{1{1'b0}}, subtractor_1_out[3:0]};  // Bit_Extender bit_extender_3
  Shifter #(.width(32)) shifter_1 (.in(bit_extender_2_out), .\dist (bit_extender_3_out), .out(shifter_1_out));
  or or_1 (or_1_out, subtractor_1_out[4], comparator_2_eq, comparator_1_eq);
  Shifter #(.width(32), .shift("lr")) shifter_2 (.in(shifter_1_out), .\dist (5'b01010), .out(shifter_2_out));
  assign buffer_1_out = shifter_2_out;  // Buffer buffer_1, 32 bits wide
  Multiplexer #(.width(32)) multiplexer_1 (
    .in0(buffer_1_out), .in1(negator_1_out), .out(multiplexer_1_out), .sel(in_1[15]));  // open: en
  Negator #(.width(32)) negator_1 (.in(shifter_2_out), .out(negator_1_out));
  Multiplexer #(.width(32)) multiplexer_2 (
    .in0(multiplexer_1_out), .in1({32{1'b0}}), .out(out_2), .sel(or_1_out));  // open: en

  // Other names for the same wires on the sheet: sign = in_1[15]

  // Notes on the sheet:
  //   exp
endmodule
