// Logisim project P0_L1_navigation_2020.circ as structural Verilog: 3 circuits, main circuit navigation
module navigation (
  input  [1:0] dir,
  input  resert,
  input  clk,
  output hit,
  output arrive
);

  wire [3:0] state_q, ts_s_0;

  ts ts (
    .state_3(state_q[3]), .state_2(state_q[2]), .state_1(state_q[1]), .state_0(state_q[0]), .dir_1(dir[1]),
    .dir_0(dir[0]), .s_3(ts_s_0[3]), .s_2(ts_s_0[2]), .s_1(ts_s_0[1]), .s_0(ts_s_0[0]));
  Register #(.width(4)) state (.D(ts_s_0), .Q(state_q), .clk(clk), .clr(resert));  // open: en
  \output  \output  (
    .state_3(state_q[3]), .state_2(state_q[2]), .state_1(state_q[1]), .state_0(state_q[0]), .hit(hit),
    .arrive(arrive));
endmodule

module ts (
  input  state_3,
  input  state_2,
  input  state_1,
  input  state_0,
  input  dir_1,
  input  dir_0,
  output s_3,
  output s_2,
  output s_1,
  output s_0
);

  wire and_1_out, and_2_out, and_3_out, and_4_out, and_5_out, and_6_out, and_7_out, and_8_out, and_9_out,
       and_10_out, and_11_out, and_12_out, and_13_out, and_14_out, and_15_out, and_16_out, and_17_out,
       and_18_out, and_19_out, and_20_out, and_21_out, and_22_out, and_23_out, and_24_out, and_25_out,
       and_26_out, and_27_out, and_28_out, not_1_out, not_2_out, not_3_out, not_4_out, not_5_out, not_6_out,
       not_7_out, not_8_out, not_9_out, not_10_out, not_11_out, not_12_out, not_13_out, not_14_out,
       not_15_out, not_16_out, not_17_out, not_18_out, not_19_out, not_20_out, not_21_out, not_22_out,
       not_23_out, not_24_out, not_25_out, not_26_out, not_27_out, not_28_out, not_29_out, not_30_out,
       not_31_out, not_32_out, not_33_out, not_34_out, not_35_out, not_36_out, not_37_out, not_38_out,
       not_39_out, not_40_out, not_41_out, not_42_out, not_43_out, not_44_out, not_45_out, not_46_out,
       not_47_out, not_48_out, not_49_out, not_50_out, not_51_out, not_52_out, not_53_out, not_54_out,
       not_55_out, not_56_out, not_57_out, not_58_out, not_59_out, not_60_out, not_61_out, not_62_out,
       not_63_out;

  not not_1 (not_1_out, state_3);
  not not_2 (not_2_out, dir_1);
  not not_3 (not_3_out, state_3);
  not not_4 (not_4_out, state_0);
  not not_5 (not_5_out, state_3);
  not not_6 (not_6_out, dir_0);
  not not_7 (not_7_out, state_2);
  not not_8 (not_8_out, dir_1);
  not not_9 (not_9_out, state_2);
  not not_10 (not_10_out, state_1);
  not not_11 (not_11_out, state_2);
  not not_12 (not_12_out, dir_0);
  not not_13 (not_13_out, state_3);
  not not_14 (not_14_out, state_1);
  not not_15 (not_15_out, dir_1);
  not not_16 (not_16_out, dir_0);
  not not_17 (not_17_out, state_3);
  not not_18 (not_18_out, dir_1);
  not not_19 (not_19_out, dir_0);
  not not_20 (not_20_out, state_2);
  not not_21 (not_21_out, dir_1);
  not not_22 (not_22_out, dir_0);
  not not_23 (not_23_out, state_3);
  not not_24 (not_24_out, state_1);
  not not_25 (not_25_out, state_3);
  not not_26 (not_26_out, state_0);
  not not_27 (not_27_out, dir_1);
  not not_28 (not_28_out, state_3);
  not not_29 (not_29_out, state_3);
  not not_30 (not_30_out, state_0);
  not not_31 (not_31_out, dir_0);
  not not_32 (not_32_out, state_2);
  not not_33 (not_33_out, state_1);
  not not_34 (not_34_out, dir_1);
  not not_35 (not_35_out, state_2);
  not not_36 (not_36_out, state_1);
  not not_37 (not_37_out, dir_0);
  not not_38 (not_38_out, state_2);
  not not_39 (not_39_out, state_3);
  not not_40 (not_40_out, state_2);
  not not_41 (not_41_out, state_2);
  not not_42 (not_42_out, dir_0);
  not not_43 (not_43_out, state_3);
  not not_44 (not_44_out, dir_0);
  not not_45 (not_45_out, state_3);
  not not_46 (not_46_out, state_1);
  not not_47 (not_47_out, dir_1);
  not not_48 (not_48_out, state_3);
  not not_49 (not_49_out, dir_1);
  not not_50 (not_50_out, state_2);
  not not_51 (not_51_out, dir_1);
  not not_52 (not_52_out, state_3);
  not not_53 (not_53_out, state_2);
  not not_54 (not_54_out, state_3);
  not not_55 (not_55_out, state_1);
  not not_56 (not_56_out, state_3);
  not not_57 (not_57_out, state_0);
  not not_58 (not_58_out, state_2);
  not not_59 (not_59_out, state_1);
  not not_60 (not_60_out, state_3);
  not not_61 (not_61_out, dir_0);
  not not_62 (not_62_out, state_2);
  not not_63 (not_63_out, dir_0);
  and and_1 (and_1_out, not_1_out, state_2, state_1, not_2_out);
  and and_2 (and_2_out, not_3_out, state_2, state_1, not_4_out, dir_0);
  and and_3 (and_3_out, not_5_out, state_2, state_1, state_0, not_6_out);
  and and_4 (and_4_out, state_3, not_7_out, not_8_out);
  and and_5 (and_5_out, state_3, not_9_out, not_10_out, dir_0);
  and and_6 (and_6_out, state_3, not_11_out, state_1, not_12_out);
  and and_7 (and_7_out, not_13_out, not_14_out, not_15_out, not_16_out);
  and and_8 (and_8_out, not_17_out, state_0, not_18_out, not_19_out);
  and and_9 (and_9_out, not_20_out, state_1, not_21_out, not_22_out);
  and and_10 (and_10_out, not_23_out, state_2, not_24_out, dir_0);
  and and_11 (and_11_out, not_25_out, state_2, not_26_out, not_27_out, dir_0);
  and and_12 (and_12_out, not_28_out, state_2, state_0, dir_1, dir_0);
  and and_13 (and_13_out, not_29_out, state_2, state_1, not_30_out, dir_1, not_31_out);
  and and_14 (and_14_out, state_3, not_32_out, not_33_out, not_34_out, dir_0);
  and and_15 (and_15_out, state_3, not_35_out, not_36_out, dir_1, not_37_out);
  and and_16 (and_16_out, state_3, not_38_out, state_1, dir_1, dir_0);
  and and_17 (and_17_out, not_39_out, not_40_out, dir_1);
  and and_18 (and_18_out, not_41_out, state_1, dir_1, not_42_out);
  and and_19 (and_19_out, not_43_out, state_1, state_0, dir_1, not_44_out);
  and and_20 (and_20_out, not_45_out, state_2, not_46_out, not_47_out);
  and and_21 (and_21_out, not_48_out, state_2, state_0, not_49_out, dir_0);
  and and_22 (and_22_out, state_3, not_50_out, state_1, not_51_out, dir_0);
  and and_23 (and_23_out, not_52_out, not_53_out, dir_0);
  and and_24 (and_24_out, not_54_out, not_55_out, dir_0);
  and and_25 (and_25_out, not_56_out, not_57_out, dir_1, dir_0);
  and and_26 (and_26_out, not_58_out, not_59_out, dir_1, dir_0);
  and and_27 (and_27_out, not_60_out, state_2, state_1, state_0, dir_1, not_61_out);
  and and_28 (and_28_out, state_3, not_62_out, state_1, dir_1, not_63_out);
  or or_1 (s_3, and_1_out, and_2_out, and_3_out, and_4_out, and_5_out, and_6_out);
  or or_2 (s_1, and_17_out, and_18_out, and_19_out, and_20_out, and_21_out, and_22_out);
  or or_3 (s_0, and_23_out, and_24_out, and_25_out, and_26_out, and_27_out, and_28_out);
  or or_4 (s_2, and_7_out, and_8_out, and_9_out, and_10_out, and_11_out, and_12_out, and_13_out, and_14_out, and_15_out, and_16_out);
endmodule

module \output  (
  input  state_3,
  input  state_2,
  input  state_1,
  input  state_0,
  output hit,
  output arrive
);

  wire and_1_out, and_2_out, and_3_out, not_1_out, not_2_out, not_3_out, not_4_out, not_5_out, not_6_out;

  not not_1 (not_1_out, state_3);
  not not_2 (not_2_out, state_1);
  and and_1 (and_1_out, not_1_out, not_2_out, state_0);
  not not_3 (not_3_out, state_2);
  and and_2 (and_2_out, not_3_out, state_1);
  and and_3 (and_3_out, state_3, not_4_out);
  not not_4 (not_4_out, state_2);
  not not_5 (not_5_out, state_1);
  not not_6 (not_6_out, state_0);
  or or_1 (hit, and_1_out, and_2_out, and_3_out);
  and and_4 (arrive, state_3, state_2, not_5_out, not_6_out);
endmodule
