// Logisim project test.circ as structural Verilog: 1 circuit, main circuit main
module main (
  input  state_2,
  input  state_1,
  input  state_0,
  input  dir_1,
  input  dir_0,
  output arrive,
  output hit,
  output s_2,
  output s_1,
  output s_0
);

  wire and_1_out, and_2_out, and_3_out, and_4_out, and_5_out, and_6_out, and_7_out, and_8_out, and_9_out,
       and_10_out, and_11_out, and_12_out, and_13_out, and_14_out, and_15_out, and_16_out, and_17_out,
       and_18_out, not_1_out, not_2_out, not_3_out, not_4_out, not_5_out, not_6_out, not_7_out, not_8_out,
       not_9_out, not_10_out, not_11_out, not_12_out, not_13_out, not_14_out, not_15_out, not_16_out,
       not_17_out, not_18_out, not_19_out, not_20_out, not_21_out, not_22_out, not_23_out, not_24_out,
       not_25_out, not_26_out, not_27_out, not_28_out, not_29_out, not_30_out, not_31_out, not_32_out,
       not_33_out, not_34_out, not_35_out, not_36_out, not_37_out, not_38_out, not_39_out, not_40_out,
       not_41_out, not_42_out, not_43_out, not_44_out, not_45_out, not_46_out;

  not not_1 (not_1_out, state_2);
  not not_2 (not_2_out, state_0);
  not not_3 (not_3_out, dir_1);
  not not_4 (not_4_out, dir_0);
  not not_5 (not_5_out, state_2);
  not not_6 (not_6_out, dir_1);
  not not_7 (not_7_out, state_2);
  not not_8 (not_8_out, state_0);
  not not_9 (not_9_out, dir_1);
  not not_10 (not_10_out, state_2);
  not not_11 (not_11_out, state_1);
  not not_12 (not_12_out, state_0);
  not not_13 (not_13_out, state_2);
  not not_14 (not_14_out, state_0);
  not not_15 (not_15_out, dir_0);
  not not_16 (not_16_out, state_2);
  not not_17 (not_17_out, state_2);
  not not_18 (not_18_out, dir_1);
  not not_19 (not_19_out, dir_0);
  not not_20 (not_20_out, state_2);
  not not_21 (not_21_out, state_0);
  not not_22 (not_22_out, dir_1);
  not not_23 (not_23_out, dir_0);
  not not_24 (not_24_out, state_2);
  not not_25 (not_25_out, dir_1);
  not not_26 (not_26_out, state_2);
  not not_27 (not_27_out, state_1);
  not not_28 (not_28_out, dir_1);
  not not_29 (not_29_out, state_2);
  not not_30 (not_30_out, dir_1);
  not not_31 (not_31_out, dir_0);
  not not_32 (not_32_out, state_2);
  not not_33 (not_33_out, state_0);
  not not_34 (not_34_out, dir_1);
  not not_35 (not_35_out, state_2);
  not not_36 (not_36_out, state_0);
  not not_37 (not_37_out, dir_0);
  not not_38 (not_38_out, state_2);
  not not_39 (not_39_out, state_2);
  not not_40 (not_40_out, state_1);
  not not_41 (not_41_out, dir_1);
  not not_42 (not_42_out, dir_0);
  not not_43 (not_43_out, state_2);
  not not_44 (not_44_out, state_2);
  not not_45 (not_45_out, state_2);
  not not_46 (not_46_out, dir_0);
  and and_1 (and_1_out, not_1_out, state_1, not_2_out, not_3_out, not_4_out);
  and and_2 (and_2_out, not_5_out, state_1, state_0, not_6_out, dir_0);
  and and_3 (and_3_out, not_7_out, not_8_out, not_9_out, dir_0);
  and and_4 (and_4_out, not_10_out, not_11_out, not_12_out, dir_1);
  and and_5 (and_5_out, not_13_out, not_14_out, dir_1, not_15_out);
  and and_6 (and_6_out, not_16_out, state_0, dir_1, dir_0);
  and and_7 (and_7_out, not_17_out, state_1, state_0, not_18_out, not_19_out);
  and and_8 (and_8_out, not_20_out, state_1, not_21_out, not_22_out, not_23_out);
  and and_9 (and_9_out, not_24_out, state_1, state_0, not_25_out, dir_0);
  and and_10 (and_10_out, not_26_out, not_27_out, state_0, not_28_out);
  and and_11 (and_11_out, not_29_out, state_0, not_30_out, not_31_out);
  and and_12 (and_12_out, not_32_out, state_1, not_33_out, not_34_out, dir_0);
  and and_13 (and_13_out, not_35_out, state_1, not_36_out, dir_1, not_37_out);
  and and_14 (and_14_out, not_38_out, state_1, state_0, dir_1, dir_0);
  and and_15 (and_15_out, not_39_out, not_40_out, not_41_out, not_42_out);
  and and_16 (and_16_out, not_43_out, state_0, dir_1, dir_0);
  and and_17 (and_17_out, not_44_out, state_1, dir_1, dir_0);
  and and_18 (and_18_out, not_45_out, state_1, state_0, not_46_out);
  or or_1 (arrive, and_1_out, and_2_out);
  or or_2 (hit, and_3_out, and_4_out, and_5_out, and_6_out, and_7_out);
  or or_3 (s_2, and_8_out, and_9_out);
  or or_4 (s_1, and_10_out, and_11_out, and_12_out, and_13_out, and_14_out);
  or or_5 (s_0, and_15_out, and_16_out, and_17_out, and_18_out);
endmodule
