// Logisim project P3_L0_2022.circ as structural Verilog: 13 circuits, main circuit main
module main (
  input  reset,
  output [31:0] Instr,
  output RegWrite,
  output [4:0] RegAddr,
  output [31:0] RegData,
  output MemWrite,
  output [4:0] MemAddr,
  output [31:0] MemData
);

  wire beq, bitselector_1_out, j, jal, jalr, lh, lui, lw, lw_sw_lh, MemWrite_t, ori, R_I, RegWrite_t, sll;
  wire [2:0] ALU_op, priority_encoder_1_out;
  wire [4:0] multiplexer_1_out, multiplexer_2_out, multiplexer_5_out, Rd, RegAdr, Rs, Rt, shamt;
  wire [5:0] func, spilitter_1_op;
  wire [15:0] imm, multiplexer_3_out;
  wire [25:0] j_address;
  wire [31:0] adder_1_out, Addr, ALU_output, bit_extender_1_out, bit_extender_2_out, bit_extender_3_out,
       bit_extender_4_out, DM_output, Instr_t, j_reg_value, MemData_t, multiplexer_8_out, multiplexer_9_out,
       npc_1_next_pc, PC, RegData_t, zero_ext_16_1_out_2;

  Multiplexer #(.width(5), .enable("false")) multiplexer_1 (.in0(Rd), .in1(Rt), .out(multiplexer_1_out), .sel(R_I));
  Multiplexer #(.width(5), .enable("false")) multiplexer_2 (
    .in0(multiplexer_1_out), .in1(Rd), .out(multiplexer_2_out), .sel(jalr));
  zero_EXT_16 zero_ext_16_1 (.in_1(imm), .out_2(zero_ext_16_1_out_2));
  Adder #(.width(32)) adder_1 (.a(PC), .b(32'h4), .out(adder_1_out));  // open: cin, cout
  Multiplexer #(.width(16)) multiplexer_3 (
    .in0(DM_output[15:0]), .in1(DM_output[31:16]), .out(multiplexer_3_out), .sel(bitselector_1_out));  // open: en
  BitSelector #(.width(32)) bitselector_1 (.in(Addr), .out(bitselector_1_out), .sel(5'b00001));
  NPC npc_1 (
    .PC(PC), .imm(imm), .ALU_output(ALU_output), .j_address(j_address), .beq(beq), .j(j),
    .next_pc(npc_1_next_pc), .j_reg_control(jalr), .j_reg(j_reg_value));
  Multiplexer #(.width(5), .enable("false")) multiplexer_4 (
    .in0(multiplexer_2_out), .in1({5{1'b1}}), .out(RegAdr), .sel(jal));
  assign bit_extender_1_out = {{16{multiplexer_3_out[15]}}, multiplexer_3_out};  // Bit_Extender bit_extender_1
  // Probe on npc_1_next_pc
  Multiplexer #(.width(5), .enable("false")) multiplexer_5 (.in0(Rs), .in1(Rt), .out(multiplexer_5_out), .sel(sll));
  // Probe on RegData_t
  // Probe on PC
  IFU ifu_1 (.next_PC(npc_1_next_pc), .Instr(Instr_t), .PC(PC), .reset(reset));
  GRF grf_1 (
    .reset(reset), .RegWrite(RegWrite_t), .A1(multiplexer_5_out), .A2(Rt), .RegAddr(RegAdr),
    .RegData(RegData_t), .RD1(j_reg_value), .RD2(MemData_t));
  spilitter spilitter_1 (
    .instruction(Instr_t), .func(func), .shamt(shamt), .Rd(Rd), .Rt(Rt), .Rs(Rs), .op(spilitter_1_op),
    .imm_16(imm), .j_address_26(j_address));
  Multiplexer #(.width(32), .enable("false")) multiplexer_6 (
    .in0(MemData_t), .in1(bit_extender_2_out), .out(Addr), .sel(lw_sw_lh));
  assign bit_extender_2_out = {{16{imm[15]}}, imm};  // Bit_Extender bit_extender_2
  Multiplexer #(.select(3), .width(32), .enable("false")) multiplexer_7 (
    .in0(DM_output), .in1(zero_ext_16_1_out_2), .in2(adder_1_out), .in3(bit_extender_1_out),
    .in4(adder_1_out), .in7(ALU_output), .out(RegData_t), .sel(priority_encoder_1_out));  // open: in5, in6
  Priority_Encoder priority_encoder_1 (
    .in0(lw), .in1(lui), .in2(jalr), .in3(lh), .in4(jal), .out(priority_encoder_1_out));  // open: in5, in6, in7, en_in, gs, en_out
  Pull_Resistor #(.pull(1)) pull_resistor_1 (.node(priority_encoder_1_out));
  assign bit_extender_3_out = {{16{1'b0}}, imm};  // Bit_Extender bit_extender_3
  controller controller_1 (
    .op(spilitter_1_op), .func(func), .R_I(R_I), .RegWrite(RegWrite_t), .lw_or_sw_or_lh(lw_sw_lh),
    .MemWrite(MemWrite_t), .beq_control(beq), .lui_control(lui), .ori_control(ori), .lw_control(lw),
    .ALU_op(ALU_op), .j_control(j), .j_reg_control(jalr), .lh_control(lh), .sll_control(sll),
    .jal_control(jal));
  Multiplexer #(.width(32), .enable("false")) multiplexer_8 (
    .in0(Addr), .in1(bit_extender_3_out), .out(multiplexer_8_out), .sel(ori));
  assign bit_extender_4_out = {{27{1'b0}}, shamt};  // Bit_Extender bit_extender_4
  ALU alu_1 (.a(j_reg_value), .b(multiplexer_9_out), .ALU_op(ALU_op), .ans(ALU_output));
  Multiplexer #(.width(32), .enable("false")) multiplexer_9 (
    .in0(multiplexer_8_out), .in1(bit_extender_4_out), .out(multiplexer_9_out), .sel(sll));
  OUTPUT output_1 (
    .Instr(Instr_t), .RegWrite(RegWrite_t), .RegAdr(RegAdr), .RegData(RegData_t), .MemWrite(MemWrite_t),
    .MemAddr_Byte(ALU_output), .MemData(MemData_t), .Instr_2(Instr), .RegWrite_2(RegWrite),
    .RegAddr(RegAddr), .RegData_2(RegData), .MemWrite_2(MemWrite), .MemAddr(MemAddr), .MemData_2(MemData));
  DM dm_1 (.MemAddr(ALU_output), .MemData(MemData_t), .MemWrite(MemWrite_t), .MemOut(DM_output), .reset(reset));

  // Other names for the same wires on the sheet: MemAddr_Byte[31:0] = ALU_output; RD2[31:0] = MemData_t

  // Notes on the sheet:
  //   jal $ra
endmodule

module controller (
  input  [5:0] op,
  input  [5:0] func,
  output R_I,
  output RegWrite,
  output lw_or_sw_or_lh,
  output MemWrite,
  output beq_control,
  output lui_control,
  output ori_control,
  output lw_control,
  output j_control,
  output j_reg_control,
  output [2:0] ALU_op,
  output lh_control,
  output sll_control,
  output jal_control
);

  wire add_out, beq_out, func_add, func_jalr, func_sll, func_sub, j_out, jalr_out, lh_out, lui_out, lw_out,
       ori_out, sll, sub_out, sw_out;
  wire [2:0] multiplexer_1_out, multiplexer_2_out, multiplexer_3_out, multiplexer_4_out, multiplexer_5_out,
       multiplexer_6_out, multiplexer_7_out;

  and add (add_out, ~op[5], ~op[4], ~op[3], ~op[2], ~op[1], ~op[0], func_add);  // AND_Gate
  and sub (sub_out, ~op[5], ~op[4], ~op[3], ~op[2], ~op[1], ~op[0], func_sub);  // AND_Gate
  Multiplexer #(.width(3), .disabled(0)) multiplexer_1 (
    .in0(3'b000), .in1(3'b000), .out(multiplexer_1_out), .sel(add_out));  // open: en
  and ori (ori_out, ~op[5], ~op[4], op[3], op[2], ~op[1], op[0]);  // AND_Gate
  Multiplexer #(.width(3), .disabled(0)) multiplexer_2 (
    .in0(3'b000), .in1(3'b001), .out(multiplexer_2_out), .sel(sub_out));  // open: en
  and lw (lw_out, op[5], ~op[4], ~op[3], ~op[2], op[1], op[0]);  // AND_Gate
  Multiplexer #(.width(3), .disabled(0)) multiplexer_3 (
    .in0(3'b000), .in1(3'b010), .out(multiplexer_3_out), .sel(ori_out));  // open: en
  and sw (sw_out, op[5], ~op[4], op[3], ~op[2], op[1], op[0]);  // AND_Gate
  Multiplexer #(.width(3), .disabled(0)) multiplexer_4 (
    .in0(3'b000), .in1(3'b000), .out(multiplexer_4_out), .sel(lw_out));  // open: en
  and beq (beq_out, ~op[5], ~op[4], ~op[3], op[2], ~op[1], ~op[0]);  // AND_Gate
  Multiplexer #(.width(3), .disabled(0)) multiplexer_5 (
    .in0(3'b000), .in1(3'b000), .out(multiplexer_5_out), .sel(sw_out));  // open: en
  and lui (lui_out, ~op[5], ~op[4], op[3], op[2], op[1], op[0]);  // AND_Gate
  Multiplexer #(.width(3), .disabled(0)) multiplexer_6 (
    .in0(3'b000), .in1(3'b011), .out(multiplexer_6_out), .sel(beq_out));  // open: en
  Multiplexer #(.width(3), .disabled(0)) multiplexer_7 (
    .in0(3'b000), .in1(3'b100), .out(multiplexer_7_out), .sel(sll));  // open: en
  and j (j_out, ~op[5], ~op[4], ~op[3], ~op[2], op[1], ~op[0]);  // AND_Gate
  and jalr (jalr_out, ~op[5], ~op[4], ~op[3], ~op[2], ~op[1], ~op[0], func_jalr);  // AND_Gate
  assign ALU_op = multiplexer_1_out | multiplexer_2_out | multiplexer_3_out | multiplexer_4_out | multiplexer_5_out | multiplexer_6_out | multiplexer_7_out;  // OR_Gate ALU_op, 3 bits wide
  and lh (lh_out, op[5], ~op[4], ~op[3], ~op[2], ~op[1], op[0]);  // AND_Gate
  and u_sll (sll, ~op[5], ~op[4], ~op[3], ~op[2], ~op[1], ~op[0], func_sll);  // AND_Gate
  and jal (jal_control, ~op[5], ~op[4], ~op[3], ~op[2], op[1], op[0]);  // AND_Gate
  or u_R_I (R_I, ori_out, lw_out, lui_out, lh_out);
  or lw_or_sw (lw_or_sw_or_lh, lw_out, sw_out, lh_out);
  buf u_MemWrite (MemWrite, sw_out);  // OR_Gate
  buf u_beq_control (beq_control, beq_out);  // OR_Gate
  buf u_lui_control (lui_control, lui_out);  // OR_Gate
  buf u_ori_control (ori_control, ori_out);  // OR_Gate
  buf u_lw_control (lw_control, lw_out);  // OR_Gate
  or u_j_control (j_control, j_out, jal_control);
  buf u_j_reg_control (j_reg_control, jalr_out);  // OR_Gate
  buf u_lh_control (lh_control, lh_out);  // OR_Gate
  buf u_sll_control (sll_control, sll);  // OR_Gate
  and u_func_add (func_add, func[5], ~func[4], ~func[3], ~func[2], ~func[1], ~func[0]);  // AND_Gate
  and func_add_2 (func_sub, func[5], ~func[4], ~func[3], ~func[2], func[1], ~func[0]);  // AND_Gate
  and u_func_jalr (func_jalr, ~func[5], ~func[4], func[2], ~func[2], ~func[1], func[0]);  // AND_Gate
  or u_RegWrite (RegWrite, jal_control, add_out, sub_out, ori_out, lw_out, lui_out, jalr_out, lh_out, sll);
  and u_func_sll (func_sll, ~func[5], ~func[4], ~func[3], ~func[2], ~func[1], ~func[0]);  // AND_Gate

  // Other names for the same wires on the sheet: jal = jal_control
endmodule

module spilitter (
  input  [31:0] instruction,
  output [5:0] func,
  output [4:0] shamt,
  output [4:0] Rd,
  output [4:0] Rt,
  output [4:0] Rs,
  output [5:0] op,
  output [15:0] imm_16,
  output [25:0] j_address_26
);


  assign func = instruction[5:0];
  assign imm_16 = instruction[15:0];
  assign j_address_26 = instruction[25:0];
  assign op = instruction[31:26];
  assign Rd = instruction[15:11];
  assign Rs = instruction[25:21];
  assign Rt = instruction[20:16];
  assign shamt = instruction[10:6];
endmodule

module NPC (
  input  [31:0] PC,
  input  [15:0] imm,
  input  [31:0] ALU_output,
  input  [25:0] j_address,
  input  [31:0] j_reg,
  input  beq,
  input  j,
  input  j_reg_control,
  output [31:0] next_pc
);

  wire bit_extender_1_out;
  wire [2:0] priority_encoder_1_out;
  wire [31:0] adder_1_out, adder_2_out, multiplexer_1_out, signed_ext_16_2_1_ext_output,
       signed_ext_26_2_1_ext_output;

  Adder #(.width(32)) adder_1 (.a(32'h4), .b(PC), .out(adder_1_out));  // open: cin, cout
  signed_EXT_16_2 signed_ext_16_2_1 (.EXT_input(imm), .EXT_output(signed_ext_16_2_1_ext_output));
  Adder #(.width(32)) adder_2 (
    .a(adder_1_out), .b(signed_ext_16_2_1_ext_output), .out(adder_2_out));  // open: cin, cout
  Multiplexer #(.width(32)) multiplexer_1 (
    .in0(adder_2_out), .in1(adder_1_out), .out(multiplexer_1_out), .sel(bit_extender_1_out));  // open: en
  Bit_Extender #(.in_width(32), .out_width(1)) bit_extender_1 (.in(ALU_output), .out(bit_extender_1_out));
  signed_EXT_26_2 signed_ext_26_2_1 (.EXT_input(j_address), .EXT_output(signed_ext_26_2_1_ext_output));
  Priority_Encoder priority_encoder_1 (
    .in0(beq), .in1(j), .in2(j_reg_control), .out(priority_encoder_1_out));  // open: in3, in4, in5, in6, in7, en_in, gs, en_out
  Multiplexer #(.select(3), .width(32)) multiplexer_2 (
    .in0(multiplexer_1_out), .in1(signed_ext_26_2_1_ext_output), .in2(j_reg), .in7(adder_1_out),
    .out(next_pc), .sel(priority_encoder_1_out));  // open: in3, in4, in5, in6, en
  // Probe on priority_encoder_1_out
  Pull_Resistor #(.pull(1)) pull_resistor_1 (.node(priority_encoder_1_out));
endmodule

module IFU (
  input  [31:0] next_PC,
  input  reset,
  output [31:0] PC,
  output [31:0] Instr
);

  wire clock_1_out;
  wire [9:0] bit_extender_1_out;
  wire [31:0] shifter_1_out;

  Clock clock_1 (.out(clock_1_out));
  Register #(.width(32)) u_PC (.D(next_PC), .Q(PC), .clk(clock_1_out), .clr(reset));  // open: en
  Shifter #(.width(32), .shift("lr")) shifter_1 (.in(PC), .\dist (5'b00010), .out(shifter_1_out));
  Bit_Extender #(.in_width(32), .out_width(10)) bit_extender_1 (.in(shifter_1_out), .out(bit_extender_1_out));
  ROM #(.addrWidth(10), .dataWidth(32)) rom_1 (.addr(bit_extender_1_out), .data(Instr));  // open: sel

  // Notes on the sheet:
  //   contents of rom_1 (hex, n*v repeats v):
  //   351d0100 c000c02 afbf0000 35ef0004 3afe822 afbe0000 35ef0004 3afe822 afbd0000 35ef0004 3afe822
  //   afbc0000 35ef0004 3afe822 afbb0000 35ef0004 3afe822 afba0000 35ef0004 3afe822 afb90000 35ef0004
  //   3afe822 afb80000 35ef0004 3afe822 afb70000 35ef0004 3afe822 afb60000 35ef0004 3afe822 afb50000
  //   35ef0004 3afe822 afb40000 35ef0004 3afe822 afb30000 35ef0004 3afe822 afb20000 35ef0004 3afe822
  //   afb10000 35ef0004 3afe822 afb00000 35ef0004 3afe822 afaf0000 35ef0004 3afe822 afae0000 35ef0004
  //   3afe822 afad0000 35ef0004 3afe822 afac0000 35ef0004 3afe822 afab0000 35ef0004 3afe822 afaa0000
  //   35ef0004 3afe822 afa90000 35ef0004 3afe822 afa80000 35ef0004 3afe822 afa70000 35ef0004 3afe822
  //   afa60000 35ef0004 3afe822 afa50000 35ef0004 3afe822 afa40000 35ef0004 3afe822 afa30000 35ef0004
  //   3afe822 afa20000 35ef0004 3afe822 afa10000 35ef0004 3afe822 afa00000 35ef0004 3afe822
endmodule

module GRF (
  input  reset,
  input  RegWrite,
  input  [4:0] A1,
  input  [4:0] A2,
  input  [4:0] RegAddr,
  input  [31:0] RegData,
  output [31:0] RD1,
  output [31:0] RD2
);

  wire clk;
  wire [31:0] in0, in1, in2, in3, in4, in5, in6, in7, in8, in9, in10, in11, in12, in13, in14, in15, in16,
       in17, in18, in19, in20, in21, in22, in23, in24, in25, in26, in27, in28, in29, in30, in31, out0, out1,
       out2, out3, out4, out5, out6, out7, out8, out9, out10, out11, out12, out13, out14, out15, out16,
       out17, out18, out19, out20, out21, out22, out23, out24, out25, out26, out27, out28, out29, out30,
       out31;

  Clock u_clk (.out(clk));
  Demultiplexer #(.select(5), .width(32), .tristate("true")) demultiplexer_1 (
    .out1(in1), .out2(in2), .out3(in3), .out4(in4), .out5(in5), .out6(in6), .out7(in7), .out8(in8),
    .out9(in9), .out10(in10), .out11(in11), .out12(in12), .out13(in13), .out14(in14), .out15(in15),
    .out16(in16), .out17(in17), .out18(in18), .out19(in19), .out20(in20), .out21(in21), .out22(in22),
    .out23(in23), .out24(in24), .out25(in25), .out26(in26), .out27(in27), .out28(in28), .out29(in29),
    .out30(in30), .out31(in31), .in(RegData), .sel(RegAddr), .en(RegWrite));  // open: out0
  Register #(.width(32)) reg0 (.D(in0), .Q(out0), .clk(clk), .clr(reset));  // open: en
  Register #(.width(32)) reg1 (.D(in1), .Q(out1), .clk(clk), .clr(reset));  // open: en
  Register #(.width(32)) reg2 (.D(in2), .Q(out2), .clk(clk), .clr(reset));  // open: en
  Register #(.width(32)) reg3 (.D(in3), .Q(out3), .clk(clk), .clr(reset));  // open: en
  Register #(.width(32)) reg4 (.D(in4), .Q(out4), .clk(clk), .clr(reset));  // open: en
  Register #(.width(32)) reg5 (.D(in5), .Q(out5), .clk(clk), .clr(reset));  // open: en
  Register #(.width(32)) reg6 (.D(in6), .Q(out6), .clk(clk), .clr(reset));  // open: en
  Register #(.width(32)) reg7 (.D(in7), .Q(out7), .clk(clk), .clr(reset));  // open: en
  Register #(.width(32)) reg8 (.D(in8), .Q(out8), .clk(clk), .clr(reset));  // open: en
  Register #(.width(32)) reg9 (.D(in9), .Q(out9), .clk(clk), .clr(reset));  // open: en
  Register #(.width(32)) reg10 (.D(in10), .Q(out10), .clk(clk), .clr(reset));  // open: en
  Register #(.width(32)) reg11 (.D(in11), .Q(out11), .clk(clk), .clr(reset));  // open: en
  Register #(.width(32)) reg12 (.D(in12), .Q(out12), .clk(clk), .clr(reset));  // open: en
  Register #(.width(32)) reg13 (.D(in13), .Q(out13), .clk(clk), .clr(reset));  // open: en
  Register #(.width(32)) reg14 (.D(in14), .Q(out14), .clk(clk), .clr(reset));  // open: en
  Register #(.width(32)) reg15 (.D(in15), .Q(out15), .clk(clk), .clr(reset));  // open: en
  Register #(.width(32)) reg16 (.D(in16), .Q(out16), .clk(clk), .clr(reset));  // open: en
  Register #(.width(32)) reg17 (.D(in17), .Q(out17), .clk(clk), .clr(reset));  // open: en
  Register #(.width(32)) reg18 (.D(in18), .Q(out18), .clk(clk), .clr(reset));  // open: en
  Register #(.width(32)) reg19 (.D(in19), .Q(out19), .clk(clk), .clr(reset));  // open: en
  Register #(.width(32)) reg20 (.D(in20), .Q(out20), .clk(clk), .clr(reset));  // open: en
  Register #(.width(32)) reg21 (.D(in21), .Q(out21), .clk(clk), .clr(reset));  // open: en
  Register #(.width(32)) reg22 (.D(in22), .Q(out22), .clk(clk), .clr(reset));  // open: en
  Register #(.width(32)) reg23 (.D(in23), .Q(out23), .clk(clk), .clr(reset));  // open: en
  Register #(.width(32)) reg24 (.D(in24), .Q(out24), .clk(clk), .clr(reset));  // open: en
  Register #(.width(32)) reg25 (.D(in25), .Q(out25), .clk(clk), .clr(reset));  // open: en
  Register #(.width(32)) reg26 (.D(in26), .Q(out26), .clk(clk), .clr(reset));  // open: en
  Register #(.width(32)) reg27 (.D(in27), .Q(out27), .clk(clk), .clr(reset));  // open: en
  Register #(.width(32)) reg28 (.D(in28), .Q(out28), .clk(clk), .clr(reset));  // open: en
  Register #(.width(32)) reg29 (.D(in29), .Q(out29), .clk(clk), .clr(reset));  // open: en
  Register #(.width(32)) reg30 (.D(in30), .Q(out30), .clk(clk), .clr(reset));  // open: en
  Register #(.width(32)) reg31 (.D(in31), .Q(out31), .clk(clk), .clr(reset));  // open: en
  Multiplexer #(.select(5), .width(32)) multiplexer_1 (
    .in0(out0), .in1(out1), .in2(out2), .in3(out3), .in4(out4), .in5(out5), .in6(out6), .in7(out7),
    .in8(out8), .in9(out9), .in10(out10), .in11(out11), .in12(out12), .in13(out13), .in14(out14),
    .in15(out15), .in16(out16), .in17(out17), .in18(out18), .in19(out19), .in20(out20), .in21(out21),
    .in22(out22), .in23(out23), .in24(out24), .in25(out25), .in26(out26), .in27(out27), .in28(out28),
    .in29(out29), .in30(out30), .in31(out31), .out(RD1), .sel(A1));  // open: en
  Multiplexer #(.select(5), .width(32)) multiplexer_2 (
    .in0(out0), .in1(out1), .in2(out2), .in3(out3), .in4(out4), .in5(out5), .in6(out6), .in7(out7),
    .in8(out8), .in9(out9), .in10(out10), .in11(out11), .in12(out12), .in13(out13), .in14(out14),
    .in15(out15), .in16(out16), .in17(out17), .in18(out18), .in19(out19), .in20(out20), .in21(out21),
    .in22(out22), .in23(out23), .in24(out24), .in25(out25), .in26(out26), .in27(out27), .in28(out28),
    .in29(out29), .in30(out30), .in31(out31), .out(RD2), .sel(A2));  // open: en
endmodule

module RegData (
  input  [31:0] ALU_output,
  input  [31:0] DM_output,
  output [31:0] RegData
);

  wire jalr, lui, lw;
  wire [15:0] imm;
  wire [31:0] adder_1_out, multiplexer_1_out, multiplexer_2_out, PC, zero_ext_16_1_out_2;

  Multiplexer #(.width(32)) multiplexer_1 (
    .in0(ALU_output), .in1(DM_output), .out(multiplexer_1_out), .sel(lw));  // open: en
  zero_EXT_16 zero_ext_16_1 (.in_1(imm), .out_2(zero_ext_16_1_out_2));
  Multiplexer #(.width(32), .enable("false")) multiplexer_2 (
    .in0(multiplexer_1_out), .in1(zero_ext_16_1_out_2), .out(multiplexer_2_out), .sel(lui));
  Adder #(.width(32)) adder_1 (.a(PC), .b(32'h4), .out(adder_1_out));  // open: cin, cout
  Multiplexer #(.width(32), .enable("false")) multiplexer_3 (
    .in0(multiplexer_2_out), .in1(adder_1_out), .out(RegData), .sel(jalr));
endmodule

module ALU (
  input  [31:0] a,
  input  [31:0] b,
  input  [2:0] ALU_op,
  output [31:0] ans
);

  wire [1:0] comparator_1_gt;
  wire [4:0] bit_extender_1_out;
  wire [31:0] adder_1_out, multiplexer_1_out, or_1_out, shifter_1_out, subtractor_1_out;

  Comparator #(.width(32)) comparator_1 (.a(a), .b(b), .gt(comparator_1_gt[0]), .lt(comparator_1_gt[1]));  // open: eq
  Bit_Extender #(.in_width(32), .out_width(5)) bit_extender_1 (.in(b), .out(bit_extender_1_out));
  Shifter #(.width(32)) shifter_1 (.in(a), .\dist (bit_extender_1_out), .out(shifter_1_out));
  Adder #(.width(32)) adder_1 (.a(a), .b(b), .out(adder_1_out));  // open: cin, cout
  Subtractor #(.width(32)) subtractor_1 (.a(a), .b(b), .out(subtractor_1_out));  // open: bin, bout
  assign or_1_out = a | b;  // OR_Gate or_1, 32 bits wide
  Multiplexer #(.select(2), .width(32), .enable("false")) multiplexer_1 (
    .in0({32{1'b0}}), .in1(32'h1), .in2(32'h11111111), .out(multiplexer_1_out), .sel(comparator_1_gt));  // open: in3
  Multiplexer #(.select(3), .width(32)) multiplexer_2 (
    .in0(adder_1_out), .in1(subtractor_1_out), .in2(or_1_out), .in3(multiplexer_1_out), .in4(shifter_1_out),
    .out(ans), .sel(ALU_op));  // open: in5, in6, in7, en
endmodule

module DM (
  input  [31:0] MemAddr,
  input  [31:0] MemData,
  input  MemWrite,
  input  reset,
  output [31:0] MemOut
);

  wire clock_1_out, not_1_out;
  wire [9:0] bit_extender_1_out;
  wire [31:0] shifter_1_out;

  Shifter #(.width(32), .shift("lr")) shifter_1 (.in(MemAddr), .\dist (5'b00010), .out(shifter_1_out));
  Bit_Extender #(.in_width(32), .out_width(10)) bit_extender_1 (.in(shifter_1_out), .out(bit_extender_1_out));
  Clock clock_1 (.out(clock_1_out));
  RAM #(.addrWidth(10), .dataWidth(32), .bus("separate")) ram_1 (
    .addr(bit_extender_1_out), .din(MemData), .data(MemOut), .str(MemWrite), .clk(clock_1_out),
    .ld(not_1_out), .clr(reset));  // open: sel
  not not_1 (not_1_out, MemWrite);
endmodule

module OUTPUT (
  input  [31:0] Instr,
  input  RegWrite,
  input  [4:0] RegAdr,
  input  [31:0] RegData,
  input  MemWrite,
  input  [31:0] MemAddr_Byte,
  input  [31:0] MemData,
  output [31:0] Instr_2,
  output RegWrite_2,
  output [4:0] RegAddr,
  output [31:0] RegData_2,
  output MemWrite_2,
  output [4:0] MemAddr,
  output [31:0] MemData_2
);

  wire [31:0] shifter_1_out;

  Shifter #(.width(32), .shift("lr")) shifter_1 (.in(MemAddr_Byte), .\dist (5'b00010), .out(shifter_1_out));
  Bit_Extender #(.in_width(32), .out_width(5)) bit_extender_1 (.in(shifter_1_out), .out(MemAddr));

  assign Instr_2 = Instr;
  assign MemData_2 = MemData;
  assign MemWrite_2 = MemWrite;
  assign RegAddr = RegAdr;
  assign RegData_2 = RegData;
  assign RegWrite_2 = RegWrite;
endmodule

module zero_EXT_16 (
  input  [15:0] in_1,
  output [31:0] out_2
);

  wire [31:0] bit_extender_1_out;

  assign bit_extender_1_out = {{16{1'b0}}, in_1};  // Bit_Extender bit_extender_1
  Shifter #(.width(32)) shifter_1 (.in(bit_extender_1_out), .\dist (5'b10000), .out(out_2));
endmodule

// signed_16+2
module signed_EXT_16_2 (
  input  [15:0] EXT_input,
  output [31:0] EXT_output
);

  assign EXT_output = {{14{EXT_input[15]}}, {EXT_input, 2'b00}};  // Bit_Extender bit_extender_1
endmodule

// signed_26+2
module signed_EXT_26_2 (
  input  [25:0] EXT_input,
  output [31:0] EXT_output
);

  assign EXT_output = {{4{EXT_input[25]}}, {EXT_input, 2'b00}};  // Bit_Extender bit_extender_1
endmodule
